# Fritzing sketch arduino TF Mini (saved by Fritzing 0.9.3b)
breadboards: 1

parts:
  Part1 = Arduino Nano (Rev3.0)
  J1 = Basic Servo  # not connected
  J3 = Dagu DGServo 9g header (male) [package=THT]
  J4 = Infrared Proximity Sensor
  Part3 = I2C level shifter bidirectional
  J5 = Dagu DGServo 9g header (male) [package=THT]

nets:
  GND: Part1.GND, Part3.GND
  N1: Part1.D3, J3.gnd
  N2: Part1.D4, J5.gnd
  N3: Part1.D9, Part3.HV4
  N4: Part1.D10, Part3.HV1
  N5: J4.Vcc, Part3.HV

notes:
  PWM Out Aux
  Lidar Sweep Servo
  TF Mini S
  TF Mini Plus
  Bi-Directional Logic converter
  5A & 5B
  3A & 3B
  PWM in RC
