# Fritzing sketch arduino TF Mini2 (saved by Fritzing 0.9.3b)

parts:
  Part1 = Arduino Nano (Rev3.0)
  J1 = Basic Servo  # not connected
  J3 = Dagu DGServo 9g header (male) [package=THT]
  J5 = Dagu DGServo 9g header (male) [package=THT]
  Part2 = Logic Level Converter
  J6 = Dagu DGServo 9g header (male) [package=THT]
  J7 = Dagu DGServo 9g header (male) [package=THT]
  J8 = Dagu DGServo 9g header (male) [package=THT]
  J9 = Dagu DGServo 9g header (male) [package=THT]
  Part3 = Bluetooth HC-05 Macho

nets:
  N1: Part1.D1/TX, Part3.RXD
  N2: Part1.D0/RX, Part3.TXD
  GND: Part1.GND, Part2.GND, Part3.GND
  N3: Part1.D3, J3.gnd
  N4: Part1.D4, J5.gnd
  N5: Part1.D7, J9.gnd
  N6: Part1.D9, Part2.RX2_HV
  N7: Part1.D10, Part2.TX_HV
  N8: Part1.D11/MOSI, J6.gnd
  N9: Part1.D12/MISO, J7.gnd
  5V: Part1.5V, Part3.VCC
  N10: Part1.D13/SCK, J8.gnd

notes:
  PWM Stop Aux
  Lidar Sweep Servo
  2ch Bi-Directional Logic
  5A & 5B
  3A & 3B
  Right ADC
  Left ADC
  Lidar PWM Activation
  Stop ADC
  PWM Steer Aux
  Bluetooth / Serial Radio
  5V Power in
  Gnd
  Synerduino Lidar 8
  (D10 = RX, D9 = TX)
  4Ch Logic
  to Arduino
  to Lidar
